# Fritzing sketch Schematics (saved by Fritzing 0.9.6b)
breadboards: 1

parts:
  HC-SR04_Sensor_1 = HC-SR04 Ultrasonic Distance Sensor
  HC-SR04_Sensor_2 = HC-SR04 Ultrasonic Distance Sensor
  HC-SR04_Sensor_3 = HC-SR04 Ultrasonic Distance Sensor
  Part1 = Arduino Mega 2560 (Rev3)
  S1 = Pushbutton [package="[THT]"]
  Part3 = HX711 Weighing Sensor Module
  LCD2 = LCD screen
  LCM1602_IIC2 = LCM1602 IIC [part_number="LCM1602 IIC" chip_label="LCM1602 IIC" package="DIP (Dual Inline) [THT]"]

nets:
  VCC: HC-SR04_Sensor_1.VCC, HC-SR04_Sensor_2.VCC, HC-SR04_Sensor_3.VCC, Part1.5V, Part3.VCC, LCM1602_IIC2.VCC
  N1: HC-SR04_Sensor_1.TRIG, Part1.D7_PWM
  N2: HC-SR04_Sensor_1.ECHO, Part1.D6_PWM
  GND: HC-SR04_Sensor_1.GND, HC-SR04_Sensor_2.GND, HC-SR04_Sensor_3.GND, Part1.GND, S1.Pin_3, S1.Pin_4, Part3.GND, LCM1602_IIC2.GND
  N3: HC-SR04_Sensor_2.TRIG, Part1.D9_PWM
  N4: HC-SR04_Sensor_2.ECHO, Part1.D8_PWM
  N5: HC-SR04_Sensor_3.TRIG, Part1.D11_PWM
  N6: HC-SR04_Sensor_3.ECHO, Part1.D10_PWM
  N7: Part1.D21/SCL, LCM1602_IIC2.SCL
  N8: Part1.D20/SDA, LCM1602_IIC2.SDA
  N9: Part1.D2_PWM, Part3.DO/RX
  N10: Part1.D3_PWM, Part3.CK/TX
  N11: Part1.D4_PWM, S1.Pin_1, S1.Pin_2
  VSS: LCD2.VSS, LCM1602_IIC2.VSS
  VDD: LCD2.VDD, LCM1602_IIC2.VDD
  N12: LCD2.V0, LCM1602_IIC2.V0
  N13: LCD2.RS, LCM1602_IIC2.RS
  N14: LCD2.R/W, LCM1602_IIC2.RW
  N15: LCD2.E, LCM1602_IIC2.E
  N16: LCD2.DB0, LCM1602_IIC2.D0
  N17: LCD2.DB1, LCM1602_IIC2.D1
  N18: LCD2.DB2, LCM1602_IIC2.D2
  N19: LCD2.DB3, LCM1602_IIC2.D3
  N20: LCD2.DB4, LCM1602_IIC2.D4
  N21: LCD2.DB5, LCM1602_IIC2.D5
  N22: LCD2.DB6, LCM1602_IIC2.D6
  N23: LCD2.DB7, LCM1602_IIC2.D7
  N24: LCD2.LED+, LCM1602_IIC2.A
  N25: LCD2.LED-, LCM1602_IIC2.K
  N26: LCM1602_IIC2.LED_A, LCM1602_IIC2.LED_B

custom parts:
  LCM1602 IIC: I2C-Module to use a 1602 or 2004 LCD on with the wire.h libory Serial LCD Modul
