# Fritzing sketch Schematics (saved by Fritzing 0.9.6b)
breadboards: 1

parts:
  HC-SR04_Sensor_1 = HC-SR04 Ultrasonic Distance Sensor
  HC-SR04_Sensor_2 = HC-SR04 Ultrasonic Distance Sensor
  HC-SR04_Sensor_3 = HC-SR04 Ultrasonic Distance Sensor
  Part2 = Arduino USB Host Shield  # not connected
  Part1 = Arduino Mega 2560 (Rev3)
  S1 = Pushbutton [package="[THT]"]  # not connected
  Part3 = HX711 Weighing Sensor Module

nets:
  VCC: HC-SR04_Sensor_1.VCC, HC-SR04_Sensor_2.VCC, HC-SR04_Sensor_3.VCC, Part1.5V, Part3.VCC
  N1: HC-SR04_Sensor_1.TRIG, Part1.D7_PWM
  N2: HC-SR04_Sensor_1.ECHO, Part1.D6_PWM
  GND: HC-SR04_Sensor_1.GND, HC-SR04_Sensor_2.GND, HC-SR04_Sensor_3.GND, Part1.GND, Part3.GND
  N3: HC-SR04_Sensor_2.TRIG, Part1.D9_PWM
  N4: HC-SR04_Sensor_2.ECHO, Part1.D8_PWM
  N5: HC-SR04_Sensor_3.TRIG, Part1.D11_PWM
  N6: HC-SR04_Sensor_3.ECHO, Part1.D10_PWM
  N7: Part1.D2_PWM, Part3.DO/RX
  N8: Part1.D3_PWM, Part3.CK/TX

notes:
  Peso hx711 confirmar ligação
  ligacao botao
